# Fritzing sketch circuit (saved by Fritzing 0.8.7b)
breadboards: 1

parts:
  Part1 = Arduino Uno (Rev3)
  LED1 = LED - 5mm [color="Green (570nm)" package="5 mm [THT]"]
  LED2 = LED - 5mm [color="Yellow (595nm)" package="5 mm [THT]"]
  LED3 = LED - 5mm [color="Red (633nm)" package="5 mm [THT]"]
  S1 = Pushbutton [package="[THT]"]
  R1 = Photocell (LDR) [package=THT]
  R2 = Resistor [tolerance=±5% resistance=220 package=THT]
  R3 = Resistor [tolerance=±5% resistance=220 package=THT]

nets:
  N1: Part1.A0, R1.pin_1, R3.Pin_0
  N2: Part1.D9_PWM, LED3.anode
  N3: Part1.D10_PWM/SS, LED2.anode
  N4: Part1.D11_PWM/MOSI, LED1.anode
  N5: Part1.D7, S1.Pin_1, S1.Pin_2, R2.Pin_0
  N6: Part1.5V, S1.Pin_3, S1.Pin_4, R1.pin_0
  N7: Part1.GND, LED1.cathode, LED2.cathode, LED3.cathode, R2.Pin_1, R3.Pin_1
